// Logisim project jrmips.circ as structural Verilog: 13 circuits, main circuit main
module main (
);

  wire clock_1_out, DecoderALU_rsorrt, DecoderALU_rtorimm, DecoderBr_branchen, DecoderBr_immextendop,
       DecoderBr_writeenable, DecoderHalt_halt, DecoderHalt_hexdisplayen, DecoderMem_memread,
       DecoderMem_memwrite, DecoderMem_swen, Fields_I_subop, not_1_out;
  wire [1:0] DecoderALU_alu, DecoderBr_branchop, DecoderMem_memtoreg;
  wire [2:0] Fields_I_rs, Fields_R_rt;
  wire [3:0] Fields_I_opcode, Fields_R_shamt, HexDisplay__0_3, HexDisplay__4_7, HexDisplay__8_11,
       HexDisplay__12_15;
  wire [7:0] Fields_I_imm;
  wire [15:0] adder_1_out, ALU_result, Branch_npc, ImmExtend_immresult, multiplexer_1_out, multiplexer_2_out,
       multiplexer_3_out, multiplexer_4_out, multiplexer_5_out, PC_q, ram_1_data, RF_read__rs, RF_read__rt,
       rom_1_data, Shifter_shiftresult;

  Register #(.width(16)) PC (.D(multiplexer_3_out), .en(DecoderHalt_halt), .Q(PC_q), .clk(clock_1_out));  // open: clr
  Clock clock_1 (.out(clock_1_out));
  Adder #(.width(16)) adder_1 (.a(16'h1), .b(PC_q), .out(adder_1_out), .cin(1'b0));  // open: cout
  ROM #(.addrWidth(16), .dataWidth(16)) rom_1 (.addr(PC_q), .data(rom_1_data), .sel(1'b1));
  Fields_I Fields_I (
    .Instruction(rom_1_data), .Subop(Fields_I_subop), .Imm(Fields_I_imm), .rs(Fields_I_rs),
    .Opcode(Fields_I_opcode));
  Fields_R Fields_R (.Imm(Fields_I_imm), .Shamt(Fields_R_shamt), .rt(Fields_R_rt));
  ImmExtend ImmExtend (
    .Imm(Fields_I_imm), .Subop(Fields_I_subop), .ImmExtendOp(DecoderBr_immextendop),
    .ImmResult(ImmExtend_immresult));
  DecoderALU DecoderALU (
    .Opcode(Fields_I_opcode), .Subop(Fields_I_subop), .ALU(DecoderALU_alu), .rtOrImm(DecoderALU_rtorimm),
    .rsOrrt(DecoderALU_rsorrt));
  DeoderBranch DecoderBr (
    .Opcode(Fields_I_opcode), .ImmExtendOp(DecoderBr_immextendop), .WriteEnable(DecoderBr_writeenable),
    .BranchOp(DecoderBr_branchop), .BranchEn(DecoderBr_branchen));
  DecoderMem DecoderMem (
    .Opcode(Fields_I_opcode), .Subop(Fields_I_subop), .MemToReg(DecoderMem_memtoreg),
    .MemWrite(DecoderMem_memwrite), .MemRead(DecoderMem_memread), .swEn(DecoderMem_swen));
  DecoderHalt DecoderHalt (.Opcode(Fields_I_opcode), .HexDisplayEn(DecoderHalt_hexdisplayen), .Halt(DecoderHalt_halt));
  Register_File RF (
    .Write_Enable(DecoderBr_writeenable), .Write_Data(multiplexer_5_out), .rs(Fields_I_rs), .rt(Fields_R_rt),
    .Read__rs(RF_read__rs), .Read__rt(RF_read__rt), .Clock(clock_1_out));
  Branch Branch (
    .rs_data(RF_read__rs), .NPC(Branch_npc), .PC___1(adder_1_out), .Imm(ImmExtend_immresult),
    .BranchOp(DecoderBr_branchop));
  Multiplexer #(.width(16), .enable("false")) multiplexer_1 (
    .in0(RF_read__rs), .in1(RF_read__rt), .out(multiplexer_1_out), .sel(DecoderALU_rsorrt));
  Multiplexer #(.width(16), .enable("false")) multiplexer_2 (
    .in0(RF_read__rt), .in1(ImmExtend_immresult), .out(multiplexer_2_out), .sel(DecoderALU_rtorimm));
  Shifter Shifter (
    .rs_data(RF_read__rs), .rt_data(RF_read__rt), .Subop(Fields_I_subop), .shamt(Fields_R_shamt),
    .ShiftResult(Shifter_shiftresult));
  ALU ALU (.InputA(multiplexer_1_out), .InputB(multiplexer_2_out), .Operation(DecoderALU_alu), .Result(ALU_result));
  Multiplexer #(.width(16), .enable("false")) multiplexer_3 (
    .in0(adder_1_out), .in1(Branch_npc), .out(multiplexer_3_out), .sel(DecoderBr_branchen));
  Multiplexer #(.width(16), .enable("false")) multiplexer_4 (
    .in0(RF_read__rt), .in1(ALU_result), .out(multiplexer_4_out), .sel(DecoderMem_swen));
  RAM #(.addrWidth(16), .dataWidth(16), .bus("separate")) ram_1 (
    .addr(multiplexer_4_out), .din(RF_read__rs), .data(ram_1_data), .str(DecoderMem_memwrite), .sel(1'b1),
    .clk(clock_1_out), .ld(DecoderMem_memread));  // open: clr
  HexDisplay HexDisplay (
    .Clock(clock_1_out), .rs_data(RF_read__rs), .en(DecoderHalt_hexdisplayen), ._0_3(HexDisplay__0_3),
    ._4_7(HexDisplay__4_7), ._8_11(HexDisplay__8_11), ._12_15(HexDisplay__12_15));
  Multiplexer #(.select(2), .width(16), .enable("false")) multiplexer_5 (
    .in0(ram_1_data), .in1(adder_1_out), .in2(ALU_result), .in3(Shifter_shiftresult),
    .out(multiplexer_5_out), .sel(DecoderMem_memtoreg));
  Hex_Digit_Display hex_digit_display_1 (.value(HexDisplay__12_15));  // open: dp
  Hex_Digit_Display hex_digit_display_2 (.value(HexDisplay__4_7));  // open: dp
  Hex_Digit_Display hex_digit_display_3 (.value(HexDisplay__8_11));  // open: dp
  not not_1 (not_1_out, DecoderHalt_halt);
  Hex_Digit_Display hex_digit_display_4 (.value(HexDisplay__0_3));  // open: dp
  LED LED (.in(not_1_out));

  // Notes on the sheet:
  //   Eunsol Yun euy9@pitt.edu
  //   PC+1
  //   ROM
  //   RAM
endmodule

module ALU (
  input  [15:0] InputA,
  input  [15:0] InputB,
  input  [1:0] Operation,
  output [15:0] Result
);

  wire [15:0] adder_1_out, and_1_out, nor_1_out, subtractor_1_out;

  Adder #(.width(16)) adder_1 (.a(InputA), .b(InputB), .out(adder_1_out), .cin(1'b0));  // open: cout
  assign and_1_out = InputA & InputB;  // AND_Gate and_1, 16 bits wide
  assign nor_1_out = ~(InputA | InputB);  // NOR_Gate nor_1, 16 bits wide
  Subtractor #(.width(16)) subtractor_1 (.a(InputA), .b(InputB), .out(subtractor_1_out), .bin(1'b0));  // open: bout
  Multiplexer #(.select(2), .width(16), .enable("false")) multiplexer_1 (
    .in0(and_1_out), .in1(nor_1_out), .in2(adder_1_out), .in3(subtractor_1_out), .out(Result), .sel(Operation));
endmodule

module Register_File (
  input  Write_Enable,
  input  Clock,
  input  [15:0] Write_Data,
  input  [2:0] rs,
  input  [2:0] rt,
  output [15:0] Read__rs,
  output [15:0] Read__rt
);

  wire and_1_out, and_2_out, and_3_out, and_4_out, and_5_out, and_6_out, and_7_out, and_8_out,
       decoder_1_out0, decoder_1_out1, decoder_1_out2, decoder_1_out3, decoder_1_out4, decoder_1_out5,
       decoder_1_out6, decoder_1_out7;
  wire [15:0] r0_q, r1_q, r2_q, r3_q, r4_q, r5_q, r6_q, r7_q;

  Decoder #(.select(3), .enable("false")) decoder_1 (
    .out0(decoder_1_out0), .out1(decoder_1_out1), .out2(decoder_1_out2), .out3(decoder_1_out3),
    .out4(decoder_1_out4), .out5(decoder_1_out5), .out6(decoder_1_out6), .out7(decoder_1_out7), .sel(rs));
  and and_1 (and_1_out, decoder_1_out0, Write_Enable);
  and and_2 (and_2_out, decoder_1_out1, Write_Enable);
  and and_3 (and_3_out, decoder_1_out2, Write_Enable);
  and and_4 (and_4_out, decoder_1_out3, Write_Enable);
  and and_5 (and_5_out, decoder_1_out4, Write_Enable);
  and and_6 (and_6_out, decoder_1_out5, Write_Enable);
  and and_7 (and_7_out, decoder_1_out6, Write_Enable);
  and and_8 (and_8_out, decoder_1_out7, Write_Enable);
  Register #(.width(16)) r0 (.D(Write_Data), .en(and_1_out), .Q(r0_q), .clk(Clock));  // open: clr
  Register #(.width(16)) r1 (.D(Write_Data), .en(and_2_out), .Q(r1_q), .clk(Clock));  // open: clr
  Register #(.width(16)) r2 (.D(Write_Data), .en(and_3_out), .Q(r2_q), .clk(Clock));  // open: clr
  Register #(.width(16)) r3 (.D(Write_Data), .en(and_4_out), .Q(r3_q), .clk(Clock));  // open: clr
  Register #(.width(16)) r4 (.D(Write_Data), .en(and_5_out), .Q(r4_q), .clk(Clock));  // open: clr
  Register #(.width(16)) r5 (.D(Write_Data), .en(and_6_out), .Q(r5_q), .clk(Clock));  // open: clr
  Register #(.width(16)) r6 (.D(Write_Data), .en(and_7_out), .Q(r6_q), .clk(Clock));  // open: clr
  Register #(.width(16)) r7 (.D(Write_Data), .en(and_8_out), .Q(r7_q), .clk(Clock));  // open: clr
  Multiplexer #(.select(3), .width(16)) multiplexer_1 (
    .in0(r0_q), .in1(r1_q), .in2(r2_q), .in3(r3_q), .in4(r4_q), .in5(r5_q), .in6(r6_q), .in7(r7_q),
    .out(Read__rs), .sel(rs));  // open: en
  Multiplexer #(.select(3), .width(16)) multiplexer_2 (
    .in0(r0_q), .in1(r1_q), .in2(r2_q), .in3(r3_q), .in4(r4_q), .in5(r5_q), .in6(r6_q), .in7(r7_q),
    .out(Read__rt), .sel(rt));  // open: en
endmodule

module Fields_I (
  input  [15:0] Instruction,
  output Subop,
  output [7:0] Imm,
  output [2:0] rs,
  output [3:0] Opcode
);


  assign Imm = Instruction[8:1];
  assign Opcode = Instruction[15:12];
  assign rs = Instruction[11:9];
  assign Subop = Instruction[0];
endmodule

module Fields_R (
  input  [7:0] Imm,
  output [3:0] Shamt,
  output [2:0] rt
);


  assign rt = Imm[7:5];
  assign Shamt = Imm[3:0];
endmodule

module HexDisplay (
  input  Clock,
  input  [15:0] rs_data,
  input  en,
  output [3:0] _0_3,
  output [3:0] _4_7,
  output [3:0] _8_11,
  output [3:0] _12_15
);

  D_Flip_Flop D_Flip_Flop0 (.clk(Clock), .D(rs_data[0]), .Q(_0_3[0]), .en(en));  // open: Qn, preset, reset
  D_Flip_Flop D_Flip_Flop1 (.clk(Clock), .D(rs_data[1]), .Q(_0_3[1]), .en(en));  // open: Qn, preset, reset
  D_Flip_Flop D_Flip_Flop2 (.clk(Clock), .D(rs_data[2]), .Q(_0_3[2]), .en(en));  // open: Qn, preset, reset
  D_Flip_Flop D_Flip_Flop3 (.clk(Clock), .D(rs_data[3]), .Q(_0_3[3]), .en(en));  // open: Qn, preset, reset
  D_Flip_Flop D_Flip_Flop4 (.clk(Clock), .D(rs_data[4]), .Q(_4_7[0]), .en(en));  // open: Qn, preset, reset
  D_Flip_Flop D_Flip_Flop5 (.clk(Clock), .D(rs_data[5]), .Q(_4_7[1]), .en(en));  // open: Qn, preset, reset
  D_Flip_Flop D_Flip_Flop6 (.clk(Clock), .D(rs_data[6]), .Q(_4_7[2]), .en(en));  // open: Qn, preset, reset
  D_Flip_Flop D_Flip_Flop7 (.clk(Clock), .D(rs_data[7]), .Q(_4_7[3]), .en(en));  // open: Qn, preset, reset
  D_Flip_Flop D_Flip_Flop8 (.clk(Clock), .D(rs_data[8]), .Q(_8_11[0]), .en(en));  // open: Qn, preset, reset
  D_Flip_Flop D_Flip_Flop9 (.clk(Clock), .D(rs_data[9]), .Q(_8_11[1]), .en(en));  // open: Qn, preset, reset
  D_Flip_Flop D_Flip_Flop10 (.clk(Clock), .D(rs_data[10]), .Q(_8_11[2]), .en(en));  // open: Qn, preset, reset
  D_Flip_Flop D_Flip_Flop11 (.clk(Clock), .D(rs_data[11]), .Q(_8_11[3]), .en(en));  // open: Qn, preset, reset
  D_Flip_Flop D_Flip_Flop12 (.clk(Clock), .D(rs_data[12]), .Q(_12_15[0]), .en(en));  // open: Qn, preset, reset
  D_Flip_Flop D_Flip_Flop13 (.clk(Clock), .D(rs_data[13]), .Q(_12_15[1]), .en(en));  // open: Qn, preset, reset
  D_Flip_Flop D_Flip_Flop14 (.clk(Clock), .D(rs_data[14]), .Q(_12_15[2]), .en(en));  // open: Qn, preset, reset
  D_Flip_Flop D_Flip_Flop15 (.clk(Clock), .D(rs_data[15]), .Q(_12_15[3]), .en(en));  // open: Qn, preset, reset
endmodule

module Branch (
  input  [15:0] PC___1,
  input  [15:0] Imm,
  input  [15:0] rs_data,
  input  [1:0] BranchOp,
  output [15:0] NPC
);

  wire nor_1_out;
  wire [15:0] multiplexer_1_out, multiplexer_2_out;

  nor nor_1 (nor_1_out, rs_data[0], rs_data[1], rs_data[2], rs_data[3], rs_data[4], rs_data[5], rs_data[6], rs_data[7], rs_data[8], rs_data[9], rs_data[10], rs_data[11], rs_data[12], rs_data[13], rs_data[14], rs_data[15]);
  Multiplexer #(.width(16), .enable("false")) multiplexer_1 (
    .in0(PC___1), .in1(Imm), .out(multiplexer_1_out), .sel(nor_1_out));
  Multiplexer #(.width(16), .enable("false")) multiplexer_2 (
    .in0(Imm), .in1(PC___1), .out(multiplexer_2_out), .sel(nor_1_out));
  Multiplexer #(.select(2), .width(16), .enable("false")) multiplexer_3 (
    .in0(multiplexer_2_out), .in1(multiplexer_1_out), .in2(Imm), .in3(rs_data), .out(NPC), .sel(BranchOp));
endmodule

module Shifter (
  input  [15:0] rs_data,
  input  [15:0] rt_data,
  input  Subop,
  input  [3:0] shamt,
  output [15:0] ShiftResult
);

  wire or_1_out;
  wire [3:0] bitselector_1_out, multiplexer_1_out;
  wire [15:0] shifter_1_out, shifter_2_out;

  BitSelector #(.width(16), .group(4)) bitselector_1 (.in(rt_data), .out(bitselector_1_out), .sel(2'b00));
  or or_1 (or_1_out, shamt[0], shamt[1], shamt[2], shamt[3]);
  Multiplexer #(.width(4)) multiplexer_1 (
    .in0(bitselector_1_out), .in1(shamt), .out(multiplexer_1_out), .sel(or_1_out));  // open: en
  Shifter_part #(.width(16)) shifter_1 (.in(rs_data), .\dist (multiplexer_1_out), .out(shifter_1_out));
  Shifter_part #(.width(16), .shift("lr")) shifter_2 (.in(rs_data), .\dist (multiplexer_1_out), .out(shifter_2_out));
  Multiplexer #(.width(16)) multiplexer_2 (
    .in0(shifter_1_out), .in1(shifter_2_out), .out(ShiftResult), .sel(Subop));  // open: en
endmodule

module ImmExtend (
  input  [7:0] Imm,
  input  Subop,
  input  ImmExtendOp,
  output [15:0] ImmResult
);

  wire not_1_out;
  wire [15:0] bit_extender_1_out, bit_extender_2_out, multiplexer_1_out;

  assign bit_extender_1_out = {{8{1'b0}}, Imm};  // Bit_Extender bit_extender_1
  assign bit_extender_2_out = {{8{Imm[7]}}, Imm};  // Bit_Extender bit_extender_2
  Multiplexer #(.width(16)) multiplexer_1 (
    .in0(bit_extender_1_out), .in1(bit_extender_2_out), .out(multiplexer_1_out), .sel(not_1_out));  // open: en
  not not_1 (not_1_out, Subop);
  Multiplexer #(.width(16)) multiplexer_2 (
    .in0(bit_extender_1_out), .in1(multiplexer_1_out), .out(ImmResult), .sel(ImmExtendOp));  // open: en
endmodule

module DecoderALU (
  input  [3:0] Opcode,
  input  Subop,
  output [1:0] ALU,
  output rtOrImm,
  output rsOrrt
);

  wire not_1_out, not_2_out, not_3_out, not_4_out;

  not not_1 (not_1_out, Opcode[2]);
  not not_2 (not_2_out, Opcode[1]);
  not not_3 (not_3_out, Opcode[0]);
  not not_4 (not_4_out, Opcode[0]);
  and and_1 (rsOrrt, Opcode[2], Opcode[1], Opcode[0]);
  and and_2 (ALU[0], not_1_out, Opcode[0], Subop);
  or or_1 (ALU[1], not_2_out, not_3_out, Opcode[2]);
  or or_2 (rtOrImm, not_4_out, Opcode[2]);
endmodule

module DeoderBranch (
  input  [3:0] Opcode,
  output ImmExtendOp,
  output WriteEnable,
  output [1:0] BranchOp,
  output BranchEn
);

  wire and_1_out, and_2_out, and_3_out, and_4_out, and_5_out, and_6_out, and_7_out, and_8_out, and_9_out,
       not_2_out, not_3_out, not_4_out, not_5_out, not_6_out, not_7_out, not_8_out, not_9_out, not_10_out,
       not_11_out, not_12_out, not_13_out, not_14_out, not_15_out;

  not not_1 (ImmExtendOp, Opcode[3]);
  not not_2 (not_2_out, Opcode[3]);
  not not_3 (not_3_out, Opcode[2]);
  not not_4 (not_4_out, Opcode[3]);
  not not_5 (not_5_out, Opcode[2]);
  not not_6 (not_6_out, Opcode[3]);
  not not_7 (not_7_out, Opcode[2]);
  not not_8 (not_8_out, Opcode[3]);
  not not_9 (not_9_out, Opcode[1]);
  not not_10 (not_10_out, Opcode[0]);
  not not_11 (not_11_out, Opcode[1]);
  not not_12 (not_12_out, Opcode[0]);
  or or_1 (BranchOp[1], Opcode[1], Opcode[2]);
  not not_13 (not_13_out, Opcode[2]);
  not not_14 (not_14_out, Opcode[1]);
  not not_15 (not_15_out, Opcode[0]);
  and and_1 (and_1_out, not_2_out, not_3_out, Opcode[0]);
  and and_2 (and_2_out, not_4_out, not_5_out, Opcode[1]);
  and and_3 (and_3_out, not_6_out, Opcode[1], Opcode[0]);
  and and_4 (and_4_out, not_7_out, Opcode[1], Opcode[0]);
  and and_5 (and_5_out, not_8_out, Opcode[2], not_9_out, not_10_out);
  and and_6 (and_6_out, not_11_out, Opcode[0]);
  and and_7 (and_7_out, Opcode[1], not_12_out);
  and and_8 (and_8_out, Opcode[3], not_13_out);
  and and_9 (and_9_out, Opcode[3], not_14_out, not_15_out);
  or or_2 (WriteEnable, and_1_out, and_2_out, and_3_out, and_4_out, and_5_out);
  or or_3 (BranchOp[0], and_6_out, and_7_out);
  or or_4 (BranchEn, and_8_out, and_9_out);
endmodule

module DecoderMem (
  input  [3:0] Opcode,
  input  Subop,
  output [1:0] MemToReg,
  output MemWrite,
  output MemRead,
  output swEn
);

  wire and_1_out, and_2_out, not_1_out, not_2_out, not_3_out, not_4_out, not_5_out, not_6_out, not_7_out,
       not_8_out, not_9_out, not_10_out, not_11_out;

  not not_1 (not_1_out, Opcode[1]);
  not not_2 (not_2_out, Opcode[0]);
  not not_3 (not_3_out, Opcode[3]);
  not not_4 (not_4_out, Opcode[2]);
  not not_5 (not_5_out, Opcode[3]);
  not not_6 (not_6_out, Opcode[3]);
  not not_7 (not_7_out, Subop);
  not not_8 (not_8_out, Opcode[2]);
  not not_9 (not_9_out, Opcode[1]);
  not not_10 (not_10_out, Opcode[0]);
  and and_1 (and_1_out, not_1_out, not_2_out);
  and and_2 (and_2_out, not_3_out, not_4_out);
  not not_11 (not_11_out, Opcode[1]);
  and and_3 (MemWrite, not_5_out, Opcode[2], Opcode[1], Opcode[0], Subop);
  and and_4 (MemRead, not_6_out, Opcode[2], Opcode[1], Opcode[0], not_7_out);
  or or_1 (swEn, not_8_out, not_9_out, not_10_out, Opcode[3]);
  or or_2 (MemToReg[0], and_1_out, Opcode[3]);
  or or_3 (MemToReg[1], and_2_out, not_11_out);
endmodule

module DecoderHalt (
  input  [3:0] Opcode,
  output HexDisplayEn,
  output Halt
);

  wire not_1_out, not_2_out, not_3_out, not_4_out, not_5_out, not_6_out, not_7_out, not_8_out;

  not not_1 (not_1_out, Opcode[3]);
  not not_2 (not_2_out, Opcode[2]);
  not not_3 (not_3_out, Opcode[1]);
  not not_4 (not_4_out, Opcode[0]);
  not not_5 (not_5_out, Opcode[3]);
  not not_6 (not_6_out, Opcode[2]);
  not not_7 (not_7_out, Opcode[1]);
  not not_8 (not_8_out, Opcode[0]);
  and and_1 (HexDisplayEn, not_1_out, not_2_out, not_3_out, not_4_out);
  or or_1 (Halt, not_5_out, not_6_out, not_7_out, not_8_out);
endmodule
